# Fritzing sketch RFM69_overview (saved by Fritzing 0.9.3b)

parts:
  Part1 = Adafruit Feather 32u4 RFM69 433/900MHz [part_number="Adafruit #3076 and #3077"]  # not connected
  Part2 = Adafruit Feather 32u4 RFM69 433/900MHz [part_number="Adafruit #3076 and #3077"]
  Raspberry_Pi_1 = Raspberry Pi 3 [part_number=RPI-3-V1.2]  # not connected
  Part3 = Adafruit TSL2561 [part_number="Adafruit #439"]

nets:
  GND: Part2.GND, Part3.GND
  +3V3: Part2.+3V3, Part3.VIN
  N1: Part2.3, Part3.SCL
  N2: Part2.2, Part3.SDA

custom parts:
  Adafruit Feather 32u4 RFM69 433/900MHz: This is the Adafruit Feather 32u4 Radio (RFM69HCW) - our take on an microcontroller packet radio transceiver with built in USB and battery charging. Its an Adafruit Feather 32u4 with a 433 or 900 MHz radio module cooked in! Great for making wireless networks that can go further than 2.4GHz 802.15.4 and similar, are more flexible than Bluetooth LE and without the high power requirements of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
  Adafruit TSL2561: The TSL2561 luminosity sensor is an advanced digital light sensor, ideal for use in a wide range of light situations. Compared to low cost CdS cells, this sensor is more precise, allowing for exact lux calculations and can be configured for different gain/timing ranges to detect light ranges from up to 0.1 - 40,000+ Lux on the fly. The best part of this sensor is that it contains both infrared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
